// Logisim project Lüfter.circ as structural Verilog: 1 circuit, main circuit main
module main (
  input  a1,
  input  a2,
  input  b1,
  input  b2,
  input  c1,
  input  c2,
  output x,
  output y
);

  wire nor_1_out, nor_2_out, nor_3_out, xor_1_out, xor_2_out, xor_3_out;

  xor xor_1 (xor_1_out, a1, a2);
  nor nor_1 (nor_1_out, a1, a2);
  xor xor_2 (xor_2_out, b1, b2);
  nor nor_2 (nor_2_out, b1, b2);
  xor xor_3 (xor_3_out, c1, c2);
  nor nor_3 (nor_3_out, c1, c2);
  or or_1 (x, xor_1_out, xor_2_out, xor_3_out);
  or or_2 (y, nor_1_out, nor_2_out, nor_3_out);

  // Notes on the sheet:
  //   Gehäuse 1
  //   Gehäuse 2
  //   Gehäuse 3
  //   Meldelampe
  //   Fehlerlampe
endmodule
